// Digital circuit 1 AND.dig as structural Verilog
module _1_AND (
  input  VCC,
  input  GND,
  input  A,
  input  B,
  input  C,
  input  D,
  output Y0
);

  wire _7408_1_pin3, _7408_1_pin6;

  PowerSupply powersupply_1 (.VDD(VCC), .GND(GND));
  _7408 _7408_1 (
    .pin1(A), .pin2(B), .pin3(_7408_1_pin3), .pin4(C), .pin5(D), .pin6(_7408_1_pin6), .pin7(GND), .pin8(Y0),
    .pin9(_7408_1_pin6), .pin10(_7408_1_pin3), .pin12(GND), .pin13(GND), .pin14(VCC));  // open: pin11

  // Notes on the sheet:
  //   VCC: default 1
endmodule
