// Digital circuit 2 NAND OR.dig as structural Verilog
module _2_NAND_OR (
  input  VCC,
  input  GND,
  input  A,
  input  B,
  input  C,
  input  D,
  output Y1
);

  wire _7400_1_pin3, _7400_1_pin11;

  PowerSupply powersupply_1 (.VDD(VCC), .GND(GND));
  _7400 _7400_1 (
    .pin1(A), .pin2(B), .pin3(_7400_1_pin3), .pin4(GND), .pin5(GND), .pin7(GND), .pin9(GND), .pin10(GND),
    .pin11(_7400_1_pin11), .pin12(D), .pin13(C), .pin14(VCC));  // open: pin6, pin8
  _7432 _7432_1 (
    .pin1(_7400_1_pin3), .pin2(_7400_1_pin11), .pin3(Y1), .pin4(GND), .pin5(GND), .pin7(GND), .pin9(GND),
    .pin10(GND), .pin12(GND), .pin13(GND), .pin14(VCC));  // open: pin6, pin8, pin11

  // Notes on the sheet:
  //   VCC: default 1
endmodule
