// Digital circuit 3 NAND OR AND.dig as structural Verilog
module _3_NAND_OR_AND (
  input  VCC,
  input  GND,
  input  A,
  input  B,
  input  C,
  input  D,
  output Y2
);

  wire _7400_1_pin3, _7432_1_pin2;

  PowerSupply powersupply_1 (.VDD(VCC), .GND(GND));
  _7400 _7400_1 (
    .pin1(A), .pin2(B), .pin3(_7400_1_pin3), .pin4(GND), .pin5(GND), .pin7(GND), .pin8(GND), .pin9(GND),
    .pin10(GND), .pin11(GND), .pin12(GND), .pin13(GND), .pin14(GND));  // open: pin6
  _7432 _7432_1 (
    .pin1(_7400_1_pin3), .pin2(_7432_1_pin2), .pin3(Y2), .pin4(GND), .pin5(GND), .pin7(GND), .pin9(GND),
    .pin10(GND), .pin12(GND), .pin13(GND), .pin14(VCC));  // open: pin6, pin8, pin11
  _7408 _7408_1 (
    .pin1(GND), .pin2(GND), .pin4(GND), .pin5(GND), .pin7(GND), .pin9(GND), .pin10(GND),
    .pin11(_7432_1_pin2), .pin12(D), .pin13(C), .pin14(VCC));  // open: pin3, pin6, pin8

  // Notes on the sheet:
  //   VCC: default 1
endmodule
