// Digital circuit 4 XOR NOR AND.dig as structural Verilog
module _4_XOR_NOR_AND (
  input  VCC,
  input  GND,
  input  A,
  input  B,
  input  D,
  input  C,
  output Y3
);

  wire _7402_1_pin13, _7486_1_pin3;

  PowerSupply powersupply_1 (.VDD(VCC), .GND(GND));
  _7486 _7486_1 (
    .pin1(A), .pin2(B), .pin3(_7486_1_pin3), .pin4(GND), .pin5(GND), .pin7(GND), .pin9(GND), .pin10(GND),
    .pin12(GND), .pin13(GND), .pin14(VCC));  // open: pin6, pin8, pin11
  _7402 _7402_1 (
    .pin2(GND), .pin3(GND), .pin5(GND), .pin6(GND), .pin7(GND), .pin8(GND), .pin9(GND), .pin11(C), .pin12(D),
    .pin13(_7402_1_pin13), .pin14(VCC));  // open: pin1, pin4, pin10
  _7408 _7408_1 (
    .pin1(_7486_1_pin3), .pin2(_7402_1_pin13), .pin3(Y3), .pin4(GND), .pin5(GND), .pin7(GND), .pin9(GND),
    .pin10(GND), .pin12(GND), .pin13(GND), .pin14(VCC));  // open: pin6, pin8, pin11

  // Notes on the sheet:
  //   VCC: default 1
endmodule
