// Digital circuit lab2_1.dig as structural Verilog
module lab2_1 (
  input  VCC,
  input  GND,
  input  A,
  input  B,
  input  _1,
  input  C,
  output Y
);

  PowerSupply powersupply_1 (.VDD(VCC), .GND(GND));
  _74153 E1 (
    .pin1(GND), .pin2(A), .pin3(B), .pin4(B), .pin5(B), .pin6(_1), .pin7(Y), .pin8(GND), .pin10(GND),
    .pin11(GND), .pin12(GND), .pin13(GND), .pin14(C), .pin15(GND), .pin16(VCC));  // open: pin9

  // Notes on the sheet:
  //   VCC: default 1
endmodule
