// Digital circuit lab2_2.dig as structural Verilog
module lab2_2 (
  input  VCC,
  input  GND,
  input  B,
  input  _0,
  input  A,
  input  _1,
  input  C,
  output Y1
);

  PowerSupply powersupply_1 (.VDD(VCC), .GND(GND));
  _74153 _74153_1 (
    .pin1(GND), .pin2(B), .pin3(_0), .pin4(_0), .pin5(A), .pin6(_1), .pin7(Y1), .pin8(GND), .pin10(GND),
    .pin11(GND), .pin12(GND), .pin13(GND), .pin14(C), .pin15(GND), .pin16(VCC));  // open: pin9

  // Notes on the sheet:
  //   VCC: default 1
endmodule
