// Digital circuit lab2_3.dig as structural Verilog
module lab2_3 (
  input  VCC,
  input  GND,
  input  A,
  input  B,
  input  Cin,
  output Cout,
  output Sum
);

  wire _7404_1_pin5, _7404_1_pin9, _7404_1_pin11, _7404_1_pin13, _7404_2_pin9, _7404_2_pin11, _7404_2_pin13,
       _7432_1_pin1, _7432_1_pin2, _7432_1_pin9, _7432_1_pin10, _7432_1_pin12, _7432_1_pin13, _7432_2_pin1,
       _7432_2_pin2, _7432_2_pin9, _7432_2_pin10, _7432_2_pin12, _7432_2_pin13;

  _7432 _7432_1 (
    .pin1(_7432_1_pin1), .pin2(_7432_1_pin2), .pin3(Cout), .pin4(GND), .pin5(GND), .pin7(GND),
    .pin8(_7432_1_pin2), .pin9(_7432_1_pin9), .pin10(_7432_1_pin10), .pin11(_7432_1_pin1),
    .pin12(_7432_1_pin12), .pin13(_7432_1_pin13), .pin14(VCC));  // open: pin6
  _7404 _7404_1 (
    .pin1(GND), .pin3(GND), .pin5(_7404_1_pin5), .pin6(_7432_1_pin9), .pin7(GND), .pin8(_7432_1_pin10),
    .pin9(_7404_1_pin9), .pin10(_7432_1_pin12), .pin11(_7404_1_pin11), .pin12(_7432_1_pin13),
    .pin13(_7404_1_pin13), .pin14(VCC));  // open: pin2, pin4
  _7432 _7432_2 (
    .pin1(_7432_2_pin1), .pin2(_7432_2_pin2), .pin3(Sum), .pin4(GND), .pin5(GND), .pin7(GND),
    .pin8(_7432_2_pin2), .pin9(_7432_2_pin9), .pin10(_7432_2_pin10), .pin11(_7432_2_pin1),
    .pin12(_7432_2_pin12), .pin13(_7432_2_pin13), .pin14(VCC));  // open: pin6
  _7404 _7404_2 (
    .pin1(GND), .pin3(GND), .pin5(_7404_1_pin9), .pin6(_7432_2_pin9), .pin7(GND), .pin8(_7432_2_pin10),
    .pin9(_7404_2_pin9), .pin10(_7432_2_pin12), .pin11(_7404_2_pin11), .pin12(_7432_2_pin13),
    .pin13(_7404_2_pin13), .pin14(VCC));  // open: pin2, pin4
  _74154 _74154_1 (
    .pin2(_7404_2_pin13), .pin3(_7404_2_pin11), .pin4(_7404_1_pin13), .pin5(_7404_2_pin9),
    .pin6(_7404_1_pin11), .pin7(_7404_1_pin5), .pin8(_7404_1_pin9), .pin12(GND), .pin18(GND), .pin19(GND),
    .pin20(GND), .pin21(Cin), .pin22(B), .pin23(A), .pin24(VCC));  // open: pin1, pin9, pin10, pin11, pin13, pin14, pin15, pin16, pin17
  PowerSupply powersupply_1 (.VDD(VCC), .GND(GND));

  // Notes on the sheet:
  //   VCC: default 1
endmodule
