// Digital circuit 1) Adder.dig as structural Verilog
module _1__Adder (
  input  VCC,
  input  GND,
  input  A4,
  input  A3,
  input  B3,
  input  B2,
  input  A2,
  input  C0,
  input  B1,
  input  A1,
  input  B4,
  output S4,
  output C4,
  output S1,
  output S3,
  output S2
);

  PowerSupply powersupply_1 (.VDD(VCC), .GND(GND));
  _7483 Full_Adder (
    .pin1(A4), .pin2(S3), .pin3(A3), .pin4(B3), .pin5(VCC), .pin6(S2), .pin7(B2), .pin8(A2), .pin9(S1),
    .pin10(A1), .pin11(B1), .pin12(GND), .pin13(C0), .pin14(C4), .pin15(S4), .pin16(B4));

  // Notes on the sheet:
  //   VCC: default 1
endmodule
