// Digital circuit 2) Subtractor.dig as structural Verilog
module _2__Subtractor (
  input  VCC,
  input  GND,
  input  A4,
  input  A3,
  input  A1,
  input  A2,
  input  B4,
  input  B3,
  input  B1,
  input  B2,
  output S3,
  output S4,
  output S1,
  output S2,
  output C4
);

  wire _1_pin3, _1_pin6, _1_pin8, _1_pin11, _2_pin1;

  PowerSupply powersupply_1 (.VDD(VCC), .GND(GND));
  _7486 _1 (
    .pin1(B4), .pin2(1'b1), .pin3(_1_pin3), .pin4(B3), .pin5(1'b1), .pin6(_1_pin6), .pin7(GND),
    .pin8(_1_pin8), .pin9(B2), .pin10(1'b1), .pin11(_1_pin11), .pin12(B1), .pin13(1'b1), .pin14(VCC));
  _7486 _2 (
    .pin1(_2_pin1), .pin2(1'b1), .pin3(C4), .pin4(GND), .pin5(GND), .pin7(GND), .pin9(GND), .pin10(GND),
    .pin12(GND), .pin13(GND), .pin14(VCC));  // open: pin6, pin8, pin11
  _7483 _7483_1 (
    .pin1(A4), .pin2(S3), .pin3(A3), .pin4(_1_pin6), .pin5(VCC), .pin6(S2), .pin7(_1_pin8), .pin8(A2),
    .pin9(S1), .pin10(A1), .pin11(_1_pin11), .pin12(GND), .pin13(1'b1), .pin14(_2_pin1), .pin15(S4),
    .pin16(_1_pin3));

  // Notes on the sheet:
  //   VCC: default 1
endmodule
