// Digital circuit 3) BCD.dig as structural Verilog
module _3__BCD (
  input  VCC,
  input  GND,
  input  A4,
  input  A3,
  input  B3,
  input  B2,
  input  A2,
  input  B4,
  input  C0,
  input  B1,
  input  A1,
  output S4,
  output S1,
  output S2,
  output S3,
  output C4
);

  wire _1_pin2, _1_pin6, _1_pin9, _1_pin14, _1_pin15, _7408_1_pin3, _7408_1_pin6, _7432_1_pin3;

  PowerSupply powersupply_1 (.VDD(VCC), .GND(GND));
  _7483 _1 (
    .pin1(A4), .pin2(_1_pin2), .pin3(A3), .pin4(B3), .pin5(VCC), .pin6(_1_pin6), .pin7(B2), .pin8(A2),
    .pin9(_1_pin9), .pin10(A1), .pin11(B1), .pin12(GND), .pin13(C0), .pin14(_1_pin14), .pin15(_1_pin15),
    .pin16(B4));
  _7408 _7408_1 (
    .pin1(_1_pin15), .pin2(_1_pin2), .pin3(_7408_1_pin3), .pin4(_1_pin15), .pin5(_1_pin6),
    .pin6(_7408_1_pin6), .pin7(GND), .pin9(GND), .pin10(GND), .pin12(GND), .pin13(GND), .pin14(VCC));  // open: pin8, pin11
  _7483 _2 (
    .pin1(1'b0), .pin2(S3), .pin3(C4), .pin4(_1_pin2), .pin5(VCC), .pin6(S2), .pin7(_1_pin6), .pin8(C4),
    .pin9(S1), .pin10(1'b0), .pin11(_1_pin9), .pin12(GND), .pin13(GND), .pin15(S4), .pin16(_1_pin15));  // open: pin14
  _7432 _7432_1 (
    .pin1(_7408_1_pin3), .pin2(_7408_1_pin6), .pin3(_7432_1_pin3), .pin4(_7432_1_pin3), .pin5(_1_pin14),
    .pin6(C4), .pin7(GND), .pin9(GND), .pin10(GND), .pin12(GND), .pin13(GND), .pin14(VCC));  // open: pin8, pin11

  // Notes on the sheet:
  //   VCC: default 1
endmodule
