// Digital circuit 4) extra credit.dig as structural Verilog
module _4__extra_credit (
  input  VCC,
  input  GND,
  input  A2,
  input  A1,
  input  C0,
  input  B1,
  input  B2,
  output S2,
  output S1,
  output C4
);

  wire Full_Adder_pin7, Full_Adder_pin11;

  PowerSupply powersupply_1 (.VDD(VCC), .GND(GND));
  _7483 Full_Adder (
    .pin1(GND), .pin2(C4), .pin3(GND), .pin4(GND), .pin5(VCC), .pin6(S2), .pin7(Full_Adder_pin7), .pin8(A2),
    .pin9(S1), .pin10(A1), .pin11(Full_Adder_pin11), .pin12(GND), .pin13(C0), .pin16(GND));  // open: pin14, pin15
  _7486 XOR (
    .pin1(B2), .pin2(C0), .pin3(Full_Adder_pin7), .pin4(B1), .pin5(C0), .pin6(Full_Adder_pin11), .pin7(GND),
    .pin9(GND), .pin10(GND), .pin12(GND), .pin13(GND), .pin14(VCC));  // open: pin8, pin11

  // Notes on the sheet:
  //   VCC: default 1
  //   C0: This is the subtraction input
  //   1 to subtract
  //   0 to add
endmodule
