// Digital circuit 1) D flip flop.dig as structural Verilog
module _1__D_flip_flop (
  input  VCC,
  input  GND,
  input  clk,
  input  CLR,
  input  D,
  input  PR,
  output Q,
  output nQ
);

  PowerSupply powersupply_1 (.VDD(VCC), .GND(GND));
  _7474 _7474_1 (
    .pin1(CLR), .pin2(D), .pin3(clk), .pin4(PR), .pin5(Q), .pin6(nQ), .pin7(GND), .pin10(GND), .pin11(GND),
    .pin12(GND), .pin13(GND), .pin14(VCC));  // open: pin8, pin9

  // Notes on the sheet:
  //   VCC: default 1
  //   PR: default 1
  //   Clock Input
  //   D Flip-Flop
endmodule
