// Digital circuit 2) JK flip flop.dig as structural Verilog
module _2__JK_flip_flop (
  input  VCC,
  input  GND,
  input  J,
  input  K,
  input  Clear,
  input  clk,
  output nQ,
  output Q
);

  PowerSupply powersupply_1 (.VDD(VCC), .GND(GND));
  _74107 _74107_1 (
    .pin1(J), .pin2(nQ), .pin3(Q), .pin4(K), .pin7(GND), .pin8(GND), .pin9(GND), .pin10(GND), .pin11(GND),
    .pin12(clk), .pin13(Clear), .pin14(VCC));  // open: pin5, pin6

  // Notes on the sheet:
  //   VCC: default 1
  //   Clear: default 1
  //   Clock Input
  //   J-K FF
endmodule
