// Digital circuit 3) MFSR 74SL74.dig as structural Verilog
module _3__MFSR_74SL74 (
  input  VCC,
  input  GND,
  input  Clear,
  input  CLK,
  input  Preset,
  input  input_1,
  input  input_2,
  input  _1_bit_input,
  input  input_3,
  input  input_4,
  input  S1,
  input  S0,
  output Y1,
  output Y2,
  output Y3,
  output Y4
);

  wire _1_pin2, _1_pin12, _2_pin2, _2_pin12;

  PowerSupply powersupply_1 (.VDD(VCC), .GND(GND));
  _7474 _1 (
    .pin1(Clear), .pin2(_1_pin2), .pin3(CLK), .pin4(Preset), .pin5(Y4), .pin7(GND), .pin9(Y3),
    .pin10(Preset), .pin11(CLK), .pin12(_1_pin12), .pin13(Clear), .pin14(VCC));  // open: pin6, pin8
  _74153 _1_2 (
    .pin1(GND), .pin2(S1), .pin3(input_4), .pin4(Y3), .pin5(_1_bit_input), .pin6(Y4), .pin7(_1_pin2),
    .pin8(GND), .pin9(_1_pin12), .pin10(Y3), .pin11(Y4), .pin12(Y2), .pin13(input_3), .pin14(S0),
    .pin15(GND), .pin16(VCC));
  _7474 _2 (
    .pin1(Clear), .pin2(_2_pin2), .pin3(CLK), .pin4(Preset), .pin5(Y2), .pin7(GND), .pin9(Y1),
    .pin10(Preset), .pin11(CLK), .pin12(_2_pin12), .pin13(Clear), .pin14(VCC));  // open: pin6, pin8
  _74153 _2_2 (
    .pin1(GND), .pin2(S1), .pin3(input_2), .pin4(Y1), .pin5(Y3), .pin6(Y2), .pin7(_2_pin2), .pin8(GND),
    .pin9(_2_pin12), .pin10(Y1), .pin11(Y2), .pin12(_1_bit_input), .pin13(input_1), .pin14(S0), .pin15(GND),
    .pin16(VCC));

  // Notes on the sheet:
  //   VCC: default 1
  //   CLK: clock
  //   S1: right
  //   S0: left
  //   Manual Clock Activation
  //   ---------------------------------->
  //   INPUTS
  //   Shift
  //   S0 on = up
  //   S1 on = down
  //   Multi-Function Shift Register
  //   OUTPUTS
endmodule
